# Fritzing sketch kobukino (saved by Fritzing 0.8.5b)
breadboards: 1

parts:
  Part1 = Arduino Uno (Rev3)
  Kobuki_12V_1_5A_power_supply = Header 2 [package=molex-1x2_lock]
  Button_speed_change = Momentary Switch [package=ksa_sealed_tac_switch]
  R_-_button_speed_change = Resistor [tolerance=±5% resistance=10k package=THT]
  R_-_LED_bump_right = Resistor [tolerance=±0.5% resistance=270 package=THT]
  R_-_LED_bump_centre = Resistor [tolerance=±0.5% resistance=270 package=THT]
  LED_speed_1 = LED - 5mm [color="Red (633nm)" package="5 mm [THT]"]
  LED_speed_2 = LED - 5mm [color="Red (633nm)" package="5 mm [THT]"]
  LED_speed_max = LED - 5mm [color="Red (633nm)" package="5 mm [THT]"]
  LED_speed_0 = LED - 5mm [color="Red (633nm)" package="5 mm [THT]"]
  LED_bump_right = LED - 5mm [color="Red (633nm)" package="5 mm [THT]"]
  LED_bump_centre = LED - 5mm [color="Red (633nm)" package="5 mm [THT]"]
  LED_bump_left = LED - 5mm [color="Red (633nm)" package="5 mm [THT]"]
  R_-_LED_speed_max = Resistor [tolerance=±5% resistance=325 package=THT]
  R_-_LED_speed_2 = Resistor [tolerance=±5% resistance=325 package=THT]
  R_-_LED_speed_1 = Resistor [tolerance=±5% resistance=325 package=THT]
  R_-_LED_speed_0 = Resistor [tolerance=±5% resistance=325 package=THT]
  R_-_LED_bump_left = Resistor [tolerance=±5% resistance=270 package=THT]
  R_-_bumper_right = Resistor [tolerance=±5% resistance=10k package=THT]
  R_-_bumper_left = Resistor [tolerance=±5% resistance=10k package=THT]
  R_-_bumper_centre = Resistor [tolerance=±5% resistance=10k package=THT]
  R_-_Wheel_drop_sensors = Resistor [tolerance=±5% resistance=10k package=THT]
  R1_-_wheel_speed_right = Resistor [tolerance=±0.5% resistance=270 package=THT]
  R2_-_wheel_speed_right = Resistor [tolerance=±0.5% resistance=270 package=THT]
  R3_-_wheel_speed_right = Resistor [tolerance=±0.5% resistance=270 package=THT]
  R2_-_wheel_speed_left = Resistor [tolerance=±0.5% resistance=270 package=THT]
  R1_-_wheel_speed_left = Resistor [tolerance=±0.5% resistance=270 package=THT]
  R3_-_wheel_speed_left = Resistor [tolerance=±0.5% resistance=270 package=THT]
  C_-_wheel_speed_right = Electrolytic Capacitor [capacitance=100µF voltage=10V package="100 mil [THT, electrolytic]"]
  C_-_wheel_speed_left = Electrolytic Capacitor [capacitance=100µF voltage=10V package="100 mil [THT, electrolytic]"]
  Kobuki_DB25_connector = F25 [package=db25]

nets (from the breadboard view):
  N1: Part1.A0, R_-_bumper_left.Pin_0, Kobuki_DB25_connector.15
  N2: Part1.A1, R_-_bumper_centre.Pin_0, Kobuki_DB25_connector.17
  N3: Part1.A2, R_-_bumper_right.Pin_0, Kobuki_DB25_connector.18
  N4: Part1.A3, R_-_Wheel_drop_sensors.Pin_0, Kobuki_DB25_connector.19
  N5: Part1.D8, LED_speed_0.anode
  N6: Part1.D9_PWM, LED_bump_centre.cathode
  N7: Part1.D10_PWM/SS, R3_-_wheel_speed_right.Pin_0
  N8: Part1.D11_PWM/MOSI, R3_-_wheel_speed_left.Pin_0
  N9: Part1.D12/MISO, LED_bump_left.cathode
  N10: Part1.D2, Button_speed_change.3, R_-_button_speed_change.Pin_1
  N11: Part1.D4, LED_bump_right.cathode
  N12: Part1.D5_PWM, LED_speed_max.anode
  N13: Part1.D6_PWM, LED_speed_2.anode
  N14: Part1.D7, LED_speed_1.anode
  N15: Part1.3V3, R_-_bumper_right.Pin_1, R_-_bumper_left.Pin_1, R_-_bumper_centre.Pin_1, R_-_Wheel_drop_sensors.Pin_1
  N16: Part1.5V, R_-_button_speed_change.Pin_0, R_-_LED_bump_left.Pin_0
  N17: Part1.GND, Kobuki_12V_1_5A_power_supply.2
  N18: Part1.VIN, Kobuki_12V_1_5A_power_supply.1
  N19: Button_speed_change.1, R_-_LED_bump_right.Pin_0, R_-_LED_bump_centre.Pin_0, R_-_LED_speed_max.Pin_1, R_-_LED_speed_2.Pin_1, R_-_LED_speed_1.Pin_1, R_-_LED_speed_0.Pin_1, R1_-_wheel_speed_right.Pin_1, R1_-_wheel_speed_left.Pin_1, C_-_wheel_speed_right.+, C_-_wheel_speed_left.+, Kobuki_DB25_connector.6, Kobuki_DB25_connector.12, Kobuki_DB25_connector.13
  N20: R_-_LED_bump_right.Pin_1, LED_bump_right.anode
  N21: R_-_LED_bump_centre.Pin_1, LED_bump_centre.anode
  N22: LED_speed_1.cathode, R_-_LED_speed_1.Pin_0
  N23: LED_speed_2.cathode, R_-_LED_speed_2.Pin_0
  N24: LED_speed_max.cathode, R_-_LED_speed_max.Pin_0
  N25: LED_speed_0.cathode, R_-_LED_speed_0.Pin_0
  N26: LED_bump_left.anode, R_-_LED_bump_left.Pin_1
  N27: R1_-_wheel_speed_right.Pin_0, R2_-_wheel_speed_right.Pin_1
  N28: R2_-_wheel_speed_right.Pin_0, R3_-_wheel_speed_right.Pin_1, C_-_wheel_speed_right.-, Kobuki_DB25_connector.10
  N29: R2_-_wheel_speed_left.Pin_0, R3_-_wheel_speed_left.Pin_1, C_-_wheel_speed_left.-, Kobuki_DB25_connector.11
  N30: R2_-_wheel_speed_left.Pin_1, R1_-_wheel_speed_left.Pin_0

notes:
  RX TX DI0 DI1 DI2 GND DI3 EX5 EX5 AI0 AI1 AI2 AI3
  GND GND EX3.3 EX3.3 GND GND DO3 DO2 DO1 GND DO0 EN
  DB25 connector
  12V 1.5A
